# Fritzing sketch AudioAlchemy v3 (saved by Fritzing 0.9.10b)
circuit board: 8.46667cm x 5.64444cm
breadboards: 1

parts:
  Raspberry_Pi_1 = Raspberry Pi 3 [part_number=RPI-3-V1.2]
  S1 = SWITCH-MOMENTARY-2 [package=tactile-pth]
  S2 = SWITCH-MOMENTARY-2 [package=tactile-pth]
  S3 = SWITCH-MOMENTARY-2 [package=tactile-pth]
  Part1 = RFID-RC522-v2

nets:
  3V3: Raspberry_Pi_1.3v3, Raspberry_Pi_1.3V3, Part1.3.3V
  N1: Raspberry_Pi_1.GIPO4, S2.1
  N2: Raspberry_Pi_1.GIPO27, S1.1
  N3: Raspberry_Pi_1.GIPO10, Part1.MOSI
  N4: Raspberry_Pi_1.GIPO9, Part1.MISO
  N5: Raspberry_Pi_1.GIPO11, Part1.SCK
  N6: Raspberry_Pi_1.GIPO8, Part1.SDA
  N7: Raspberry_Pi_1.GIPO25, Part1.RST
  GND: Raspberry_Pi_1.GND, S1.2, S2.2, S3.2, Part1.GND
  N8: Raspberry_Pi_1.GIPO23, S3.1

notes:
  GPIO 23 Prev
  GPIO 4 Pause
  GPIO 27 Next

custom parts:
  RFID-RC522-v2: A simple China made RFID-RC522 Reader; do check the pin labels, as this is a MFRC522 based clone.
