# Fritzing sketch initial circuit (saved by Fritzing 1.0.2b)
breadboards: 1

parts:
  Mod1 = Raspberry Pi 4B
  S2 = Pushbutton [package="[THT]"]

nets:
  N1: Mod1.GND, S2.Pin_3, S2.Pin_4
  N2: Mod1.GPIO4, S2.Pin_1, S2.Pin_2
